# Fritzing sketch LearnCbot_mini (saved by Fritzing 0.9.0b)
breadboards: 1

parts:
  R1 = Resistor [tolerance=±5% resistance=220 package=THT]
  R2 = Resistor [tolerance=±5% resistance=220 package=THT]
  R3 = Resistor [tolerance=±5% resistance=10k package=THT]
  R4 = Resistor [tolerance=±5% resistance=10k package=THT]
  LED1 = LED - 5mm [color="Red (633nm)" package="5 mm [THT]"]
  LED2 = LED - 5mm [color="Red (633nm)" package="5 mm [THT]"]
  LED3 = LED - 5mm [color="Green (570nm)" package="5 mm [THT]"]
  LED4 = LED - 5mm [color="Green (570nm)" package="5 mm [THT]"]
  S1 = Pushbutton [package="[THT]"]
  S2 = Pushbutton [package="[THT]"]
  Parte1 = Arduino Uno (Rev3)
  R5 = Resistor [tolerance=±5% resistance=10k package=THT]
  R6 = Resistor [tolerance=±5% resistance=10k package=THT]
  J1 = Piezo Speaker
  R7 = Resistor [tolerance=±5% resistance=220 package=THT]
  Q1 = NPN-Transistor [package="TO92 [THT]"]
  R8 = Resistor [tolerance=±5% resistance=220 package=THT]

nets:
  N1: R1.Pin_0, LED3.anode
  N2: R1.Pin_1, Parte1.D5_PWM
  N3: R2.Pin_0, LED4.anode
  N4: R2.Pin_1, Parte1.D6_PWM
  N5: R3.Pin_0, LED1.anode
  N6: R3.Pin_1, Parte1.D4
  N7: R4.Pin_0, LED2.anode
  N8: R4.Pin_1, Parte1.D7
  N9: LED1.cathode, LED2.cathode, LED3.cathode, LED4.cathode, S1.Pin_3, S1.Pin_4, S2.Pin_3, S2.Pin_4, Parte1.GND, Q1.C
  N10: S1.Pin_1, S1.Pin_2, Parte1.D2, R5.Pin_0
  N11: S2.Pin_1, S2.Pin_2, Parte1.D3_PWM, R6.Pin_0
  N12: Parte1.D1/TX, R8.Pin_1
  N13: Parte1.5V, R5.Pin_1, R6.Pin_1, R7.Pin_0
  N14: J1.pin1, Q1.E
  N15: J1.pin2, R7.Pin_1
  N16: Q1.B, R8.Pin_0
